# Fritzing sketch schematic (saved by Fritzing 0.9.3b)
breadboards: 1

parts:
  Flex_sensor_-_index = Basic Flex Resistor
  Slide_potentiometer = Slide Potentiometer [maximum_resistance=10kΩ]
  Battery = LIPO-2000mAh [package=lipo-2000]
  Battery_charge_circuit = Power Cell LiPo Charger/Booster
  Power_switch = Header 2 [package=r_sw_th]
  uC = Arduino Nano (Rev3.0) (ICSP)
  Flex_sensor_-_middle = Basic Flex Resistor
  Flex_sensor_-_thumb = Basic Flex Resistor
  Flex_sensor_-_pinky = Basic Flex Resistor
  R1 = Resistor [tolerance=±5% resistance=47k package="0603 [SMD]"]
  R2 = Resistor [tolerance=±5% resistance=47k package="0603 [SMD]"]
  R5 = Resistor [tolerance=±5% resistance=47k package="0603 [SMD]"]
  R3 = Resistor [tolerance=±5% resistance=47k package="0603 [SMD]"]
  USB_charging_connector = USB Connectors [package=usb-minib]
  Pressure_sensor_-_thumb = Basic Force Sensing Resistor (FSR) [package=THT]
  Pressure_sensor_-_index = Basic Force Sensing Resistor (FSR) [package=THT]
  R7 = Resistor [tolerance=±5% resistance=3.3k package="0603 [SMD]"]
  R6 = Resistor [tolerance=±5% resistance=3.3k package="0603 [SMD]"]
  SN754410_H-Bridge = H-Bridge [package=THT]
  Stepper_motor = Stepper Motor - Bipolar
  Flex_sensor_-_ring = Basic Flex Resistor
  R4 = Resistor [tolerance=±5% resistance=47k package="0603 [SMD]"]
  12V_boost_converter = Breadboard Power Supply Board SMD

nets:
  N1: Flex_sensor_-_index.Pin_2, Slide_potentiometer.leg2, uC.5V, Flex_sensor_-_middle.Pin_2, Flex_sensor_-_thumb.Pin_2, Flex_sensor_-_pinky.Pin_2, Pressure_sensor_-_thumb.pin_0, Pressure_sensor_-_index.pin_0, SN754410_H-Bridge.1_2EN, SN754410_H-Bridge.3_4EN, SN754410_H-Bridge.VCC1, Flex_sensor_-_ring.Pin_2
  N2: Flex_sensor_-_index.pin_1, uC.A2, R2.Pin_1
  GND: Slide_potentiometer.leg1, Battery.-, Battery_charge_circuit.GND, uC.GND, R1.Pin_0, R2.Pin_0, R5.Pin_0, R3.Pin_0, USB_charging_connector.GND, R7.Pin_0, R6.Pin_0, SN754410_H-Bridge.GND1, R4.Pin_0, 12V_boost_converter.GND
  N3: Slide_potentiometer.wiper, uC.A0
  N4: Battery.+, Battery_charge_circuit.VBATT
  N5: Battery_charge_circuit.VCC, Power_switch.1
  N6: Battery_charge_circuit.5VIN, USB_charging_connector.D+
  VIN: Power_switch.2, uC.VIN, 12V_boost_converter.VIN
  N7: uC.D7, SN754410_H-Bridge.3A
  N8: uC.D8, SN754410_H-Bridge.4Y
  N9: uC.D9, SN754410_H-Bridge.2A
  N10: uC.D10, SN754410_H-Bridge.1A
  N11: uC.A7, Pressure_sensor_-_index.pin_1, R7.Pin_1
  N12: uC.A6, Pressure_sensor_-_thumb.pin_1, R6.Pin_1
  N13: uC.A5, Flex_sensor_-_pinky.pin_1, R5.Pin_1
  N14: uC.A4, Flex_sensor_-_ring.pin_1, R4.Pin_1
  N15: uC.A3, Flex_sensor_-_middle.pin_1, R3.Pin_1
  N16: uC.A1, Flex_sensor_-_thumb.pin_1, R1.Pin_1
  N17: SN754410_H-Bridge.1Y, Stepper_motor.C
  N18: SN754410_H-Bridge.2Y, Stepper_motor.A
  N19: SN754410_H-Bridge.VCC2, 12V_boost_converter.VCC
  N20: SN754410_H-Bridge.3Y, Stepper_motor.D
  N21: SN754410_H-Bridge.4A, Stepper_motor.B
